# Fritzing sketch Spooly (saved by Fritzing 1.0.6)

parts:
  CUI-enc1 = AMT103
  CUI-enc2 = AMT103
  M1 = DC Motor [voltage_(max)=6V voltage_(min)=3V]
  M2 = DC Motor [voltage_(max)=6V voltage_(min)=3V]
  Mod1 = dfr romeo mini ESP32
  VCC2 = 4 x AAA Battery Mount [internal_resistance=0.1Ω]
  VCC3 = 4 x AAA Battery Mount [internal_resistance=0.1Ω]
  S1 = Taiway 100-SP-X-T1 SPDT Miniature Toggle Switch [part_number=100-SP-X-T1-0-0-B1-M2 package=THT]
  F1 = FUSE [package=fuse_5mm]
  J1 = XT60 Connector [package=THT]
  Part1 = Adafruit BNO085 9-DOF Orientation IMU Fusion [part_number="Addfruit #4754"]
  A1 = HOTRC-DS600

nets (from the breadboard view):
  N1: CUI-enc1.B, Mod1.7
  5V: CUI-enc1.5V, CUI-enc2.5V, Mod1.3V3, Mod1.VCC, Mod1.Vin+, S1.L2, Part1.VCC, A1.Pin_1, A1.Pin_4, A1.Pin_13
  N2: CUI-enc1.A, Mod1.6
  GND: CUI-enc1.GND, CUI-enc2.GND, Mod1.GND, Mod1.Vin-, VCC3.-, J1.GND, Part1.GND, A1.Pin_2, A1.Pin_5, A1.Pin_14
  N3: CUI-enc2.B, Mod1.21
  N4: CUI-enc2.A, Mod1.20
  N5: M1.pin_1, Mod1.M1+
  N6: M1.pin_2, Mod1.M1-
  N7: M2.pin_1, Mod1.M2-
  N8: M2.pin_2, Mod1.M2+
  N9: Mod1.8, Part1.SDA/MISO/TX
  N10: Mod1.9, Part1.SCL/SCK/RX
  N11: Mod1.3, A1.Pin_21
  N12: Mod1.4, A1.Pin_18
  N13: Mod1.5, A1.Pin_15
  N14: VCC2.-, VCC3.+
  N15: VCC2.+, F1.2
  N16: S1.COM, F1.1
  N17: S1.L1, J1.VCC

notes:
  Charge Socket XT30
  Batteries should be 2 x 6V NiMh SC Hump Back Packs
  25D Motors with 9.7:1 Gear Box & 48CPR Encoders Fitted
  PWM Receiver of your choice
  AdaFruit BNO085 IMU
  DFRobot Romeo Mini ESP32

custom parts:
  dfr romeo mini ESP32: DFRobot Romeo ble mini cpu motor driver module. Pcb view has been suppressed as not needed.
  XT60 Connector: Yellow XT60 connector for high current loads up to 40A
  HOTRC-DS600: HOTRC 6 Channel F-06A F-06AT 6CH Gyro 2.4Ghz Receiver.
